// Logisim project rcd.circ as structural Verilog: 1 circuit, main circuit main
module main (
  input  [9:0] in_1,
  input  [7:0] in_2,
  input  in_3
);

  wire button_1_out, clock_1_out, not_1_out;
  wire [4:0] rom_1_data;
  wire [7:0] counter_1_q, main_1_out_5, main_2_to_a, main_2_to_b, main_2_to_c, main_3_out_3, main_4_out_3,
       main_5_out_3, main_6_out_3, main_7_out_3, main_8_out_3, main_9_out_3, main_10_out_3, main_11_out_5,
       main_12_out_5, main_13_out_8, main_13_out_9, main_13_out_10, main_14_out_8, main_14_out_9,
       main_14_out_10, main_15_out_8, main_15_out_9, main_15_out_10, main_16_out_8, main_16_out_9,
       main_16_out_10, main_17_out_8, main_17_out_9, main_17_out_10, main_18_out_8, main_18_out_9,
       main_18_out_10, main_19_out_8, main_19_out_9, main_19_out_10, main_20_out_8, main_20_out_9,
       main_20_out_10, main_21_out_8, main_21_out_9, main_21_out_10;
  wire [9:0] rom_2_data;
  wire [29:10] rom_2_data_2;

  Button button_1 (.out(button_1_out));
  not not_1 (not_1_out, in_3);
  Clock clock_1 (.out(clock_1_out));
  Counter counter_1 (
    .load(in_3), .D(in_2), .count(not_1_out), .Q(counter_1_q), .clk(clock_1_out), .clr(button_1_out));  // open: carry
  ROM #(.dataWidth(5)) rom_1 (.addr(counter_1_q), .data(rom_1_data));  // open: sel
  ROM #(.dataWidth(30)) rom_2 (.addr(counter_1_q), .data({rom_2_data_2, rom_2_data}));  // open: sel
  RAM_main main_1 (
    .out_5(main_1_out_5), .in_1(rom_2_data_2[29:20]), .in_2(clock_1_out), .in_3(main_21_out_8),
    .in_4(button_1_out));
  VAL_TRNSFR_main main_2 (
    .Inp_A(main_1_out_5), .Inp_C(main_12_out_5), .Inp_B(main_11_out_5), .To_B(main_2_to_b),
    .To_A(main_2_to_a), .To_C(main_2_to_c));
  SFTRGT_main main_3 (.in_1(main_1_out_5), .in_2(main_11_out_5), .out_3(main_3_out_3));
  SFTLFT_main main_4 (.in_1(main_1_out_5), .in_2(main_11_out_5), .out_3(main_4_out_3));
  XNOR_main main_5 (.in_1(main_1_out_5), .in_2(main_11_out_5), .out_3(main_5_out_3));
  XOR_main main_6 (.in_1(main_1_out_5), .in_2(main_11_out_5), .out_3(main_6_out_3));
  NOR_main main_7 (.in_1(main_1_out_5), .in_2(main_11_out_5), .out_3(main_7_out_3));
  NAND_main main_8 (.in_1(main_1_out_5), .in_2(main_11_out_5), .out_3(main_8_out_3));
  OR_main main_9 (.in_1(main_1_out_5), .in_2(main_11_out_5), .out_3(main_9_out_3));
  AND_main main_10 (.in_1(main_1_out_5), .in_2(main_11_out_5), .out_3(main_10_out_3));
  RAM_main main_11 (
    .out_5(main_11_out_5), .in_1(rom_2_data_2[19:10]), .in_2(clock_1_out), .in_3(main_21_out_9),
    .in_4(button_1_out));
  RAM_main main_12 (
    .out_5(main_12_out_5), .in_1(rom_2_data), .in_2(clock_1_out), .in_3(main_21_out_10), .in_4(button_1_out));
  INP_SEL_main main_13 (
    .in_1({8{1'b0}}), .in_2({8{1'b0}}), .in_3({8{1'b0}}), .in_4(in_1[8]), .out_8(main_13_out_8),
    .out_9(main_13_out_9), .out_10(main_13_out_10), .in_5(main_2_to_a), .in_6(main_2_to_b), .in_7(main_2_to_c));
  INP_SEL_main main_14 (
    .in_1(main_13_out_8), .in_2(main_13_out_9), .in_3(main_13_out_10), .in_4(in_1[7]), .out_8(main_14_out_8),
    .out_9(main_14_out_9), .out_10(main_14_out_10), .in_5({8{1'b0}}), .in_6({8{1'b0}}), .in_7(main_3_out_3));
  INP_SEL_main main_15 (
    .in_1(main_14_out_8), .in_2(main_14_out_9), .in_3(main_14_out_10), .in_4(in_1[6]), .out_8(main_15_out_8),
    .out_9(main_15_out_9), .out_10(main_15_out_10), .in_5({8{1'b0}}), .in_6({8{1'b0}}), .in_7(main_4_out_3));
  INP_SEL_main main_16 (
    .in_1(main_15_out_8), .in_2(main_15_out_9), .in_3(main_15_out_10), .in_4(in_1[5]), .out_8(main_16_out_8),
    .out_9(main_16_out_9), .out_10(main_16_out_10), .in_5({8{1'b0}}), .in_6({8{1'b0}}), .in_7(main_5_out_3));
  INP_SEL_main main_17 (
    .in_1(main_16_out_8), .in_2(main_16_out_9), .in_3(main_16_out_10), .in_4(in_1[4]), .out_8(main_17_out_8),
    .out_9(main_17_out_9), .out_10(main_17_out_10), .in_5({8{1'b0}}), .in_6({8{1'b0}}), .in_7(main_6_out_3));
  INP_SEL_main main_18 (
    .in_1(main_17_out_8), .in_2(main_17_out_9), .in_3(main_17_out_10), .in_4(in_1[3]), .out_8(main_18_out_8),
    .out_9(main_18_out_9), .out_10(main_18_out_10), .in_5({8{1'b0}}), .in_6({8{1'b0}}), .in_7(main_7_out_3));
  INP_SEL_main main_19 (
    .in_1(main_18_out_8), .in_2(main_18_out_9), .in_3(main_18_out_10), .in_4(in_1[2]), .out_8(main_19_out_8),
    .out_9(main_19_out_9), .out_10(main_19_out_10), .in_5({8{1'b0}}), .in_6({8{1'b0}}), .in_7(main_8_out_3));
  INP_SEL_main main_20 (
    .in_1(main_19_out_8), .in_2(main_19_out_9), .in_3(main_19_out_10), .in_4(in_1[1]), .out_8(main_20_out_8),
    .out_9(main_20_out_9), .out_10(main_20_out_10), .in_5({8{1'b0}}), .in_6({8{1'b0}}), .in_7(main_9_out_3));
  INP_SEL_main main_21 (
    .in_1(main_20_out_8), .in_2(main_20_out_9), .in_3(main_20_out_10), .in_4(in_1[0]), .out_8(main_21_out_8),
    .out_9(main_21_out_9), .out_10(main_21_out_10), .in_5({8{1'b0}}), .in_6({8{1'b0}}), .in_7(main_10_out_3));
endmodule
